# Fritzing sketch Schematic (saved by Fritzing 0.9.4)
breadboards: 1

parts:
  Part1 = OLED Monochrome 128x64 0.96 inch [part_number=326]
  Part2 = I2C Non-Volatile FRAM 32KB
  Part3 = ALSPT19315C
  Part4 = Arduino Uno (Rev3) - ICSP

nets:
  N1: Part1.MOSI_SDA, Part2.SDA, Part4.A4/SDA
  N2: Part1.SCLK_SCK, Part2.SCL, Part4.A5/SCL
  N3: Part1.RESET, Part4.D4
  VIN: Part1.VIN, Part4.5V
  GND: Part1.GND, Part2.GND, Part3.GND, Part4.GND
  VCC: Part2.VCC, Part3.VCC, Part4.AREF, Part4.3V3
  N4: Part3.OUT, Part4.A0

custom parts:
  OLED Monochrome 128x64 0.96 inch: These displays are small, only about 1" diameter, but very readable due to the high contrast of an OLED display. This display is made of 128x64 individual white OLED pixels, each one is turned on or off by the controller chip. Because the display makes its own light, no backlight is required. This reduces the power required to run the OLED and is why the display has such high contrast; we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
  I2C Non-Volatile FRAM 32KB: With our I2C FRAM breakout board you can add some FRAM storage to your next DIY project. FRAM allows for a lower power usage and a faster write performance. It's excellent for low-power or inconsistent-power datalogging or data buffering where you want to stream data fast while also keeping the data when there's no power. Unlike Flash or EEPROM there's no pages to worry about. Each byte can be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
  ALSPT19315C: Add a teeny analog light sensor, the ALS PT19 analog light sensor is a great way to upgrade a project that uses a photocell and needs RoHS compliance. Due to the high rejection ratio of infrared radiation, the spectral response of the ambient light sensor is close to that of human eyes. It's a pretty simple sensor - connect - to ground, + to 2.5V-5.5V or so to power it. Now measure the analog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
